// Logisim project MiniRISCV.circ as structural Verilog
module main (
  input  in_1,
  input  [3:0] in_2,
  input  in_3,
  input  in_4,
  input  in_5,
  input  in_6
);

  wire clock_1_out, comparator_black_box_1_p4, nor_1_out, or_1_out, or_2_out, or_3_out;
  wire [1:0] bypass_black_box_1_p7, bypass_black_box_1_p8;
  wire [3:0] decode_black_box_1_p6, ex_mem_1_op_o, id_ex_1_op_o, multiplexer_5_out;
  wire [4:0] bypass_black_box_1_p4, decode_black_box_1_p2, decode_black_box_1_p3, decode_black_box_1_p4,
       id_ex_1_rd_o, id_ex_1_rs1_o, id_ex_1_rs2_o, multiplexer_7_out, registerfile_1_p4, sa_1_out_2;
  wire [11:0] decode_black_box_1_p29;
  wire [19:0] bit_extender_2_out;
  wire [21:0] decode_black_box_1_p7, id_ex_1_ctrl_a_o;
  wire [31:0] adder_1_out, alu_1_p5, bit_extender_1_out, comparator_black_box_1_p2, decode_black_box_1_p5,
       ex_mem_1_alu_res_o, ex_mem_1_b_o, id_ex_1_a_o, id_ex_1_b_o, id_ex_1_imm_o, id_ex_1_pc_o,
       if_id_1_inst_o, if_id_1_pc_o, mem_wb_1_d_o, mem_wb_1_m_o, multiplexer_1_out, multiplexer_2_out,
       multiplexer_4_out, multiplexer_6_out, multiplexer_8_out, pc_1_pc, pc_1_pc_4, ram_1_data,
       registerfile_1_p1, registerfile_1_p7, registerfile_1_p8, risc_vprogramrom_1_p2;

  PC pc_1 (.we(in_5), .clk(clock_1_out), .clr(in_6), .PC_4(pc_1_pc_4), .PC(pc_1_pc));
  Clock clock_1 (.out(clock_1_out));
  // RISC_VProgramROM risc_vprogramrom_1: pin names not known; wires that end beside it: pc_1_pc, risc_vprogramrom_1_p2
  IF_ID if_id_1 (
    .inst(risc_vprogramrom_1_p2), .clk(clock_1_out), .PC4(pc_1_pc_4), .inst_o(if_id_1_inst_o),
    .PC_o(if_id_1_pc_o));
  // Decode_Black_Box decode_black_box_1: pin names not known; wires that end beside it: if_id_1_inst_o, decode_black_box_1_p2, decode_black_box_1_p3, decode_black_box_1_p4, decode_black_box_1_p5, decode_black_box_1_p6, decode_black_box_1_p7[0], decode_black_box_1_p7[1], decode_black_box_1_p7[2], decode_black_box_1_p7[3], decode_black_box_1_p7[4], decode_black_box_1_p7[5], decode_black_box_1_p7[6], decode_black_box_1_p7[7], decode_black_box_1_p7[8], decode_black_box_1_p7[9], decode_black_box_1_p7[10], decode_black_box_1_p7[11], decode_black_box_1_p7[12], decode_black_box_1_p7[13], decode_black_box_1_p7[14], decode_black_box_1_p7[15], decode_black_box_1_p7[16], decode_black_box_1_p7[17], decode_black_box_1_p7[18], decode_black_box_1_p7[19], decode_black_box_1_p7[20], decode_black_box_1_p7[21], decode_black_box_1_p29[0], decode_black_box_1_p29[1], decode_black_box_1_p29[2], decode_black_box_1_p29[3], decode_black_box_1_p29[4], decode_black_box_1_p29[5], decode_black_box_1_p29[6], decode_black_box_1_p29[7], decode_black_box_1_p29[8]
  // RegisterFile registerfile_1: pin names not known; wires that end beside it: registerfile_1_p1, clock_1_out, 1'b1, registerfile_1_p4, decode_black_box_1_p2, decode_black_box_1_p3, registerfile_1_p7, registerfile_1_p8
  ID_EX id_ex_1 (
    .clk(clock_1_out), .PC_4(if_id_1_pc_o), .A(registerfile_1_p7), .B(registerfile_1_p8),
    .imm(decode_black_box_1_p5), .ctrl_A(decode_black_box_1_p7), .ctrl_B(decode_black_box_1_p29),
    .Rd(decode_black_box_1_p4), .op(decode_black_box_1_p6), .rs1(decode_black_box_1_p2),
    .rs2(decode_black_box_1_p3), .PC_o(id_ex_1_pc_o), .A_o(id_ex_1_a_o), .B_o(id_ex_1_b_o),
    .imm_o(id_ex_1_imm_o), .ctrl_A_o(id_ex_1_ctrl_a_o), .Rd_o(id_ex_1_rd_o), .op_o(id_ex_1_op_o),
    .rs1_o(id_ex_1_rs1_o), .rs2_o(id_ex_1_rs2_o));  // open: ctrl_B_o
  // Bypass_Black_Box bypass_black_box_1: pin names not known; wires that end beside it: id_ex_1_rs1_o, id_ex_1_rs2_o, 1'b1, bypass_black_box_1_p4, 1'b1, registerfile_1_p4, bypass_black_box_1_p7, bypass_black_box_1_p8
  or or_1 (or_1_out, id_ex_1_ctrl_a_o[1], id_ex_1_ctrl_a_o[5], id_ex_1_ctrl_a_o[7], id_ex_1_ctrl_a_o[9], id_ex_1_ctrl_a_o[11], id_ex_1_ctrl_a_o[13], id_ex_1_ctrl_a_o[15], id_ex_1_ctrl_a_o[17], id_ex_1_ctrl_a_o[19]);
  nor nor_1 (nor_1_out, id_ex_1_ctrl_a_o[12], id_ex_1_ctrl_a_o[13]);
  or or_2 (or_2_out, id_ex_1_ctrl_a_o[10], id_ex_1_ctrl_a_o[11], id_ex_1_ctrl_a_o[12], id_ex_1_ctrl_a_o[13]);
  Multiplexer #(.width(32), .enable("false")) multiplexer_1 (
    .in0(id_ex_1_a_o), .in1(id_ex_1_imm_o), .out(multiplexer_1_out), .sel(or_3_out));
  Multiplexer #(.width(32), .enable("false")) multiplexer_2 (
    .in0(id_ex_1_b_o), .in1(id_ex_1_imm_o), .out(multiplexer_2_out), .sel(or_1_out));
  or or_3 (or_3_out, id_ex_1_ctrl_a_o[20], id_ex_1_ctrl_a_o[21]);
  Multiplexer #(.select(2), .width(32), .enable("false")) multiplexer_3 (
    .in0(multiplexer_2_out), .in1(registerfile_1_p1), .in2(ex_mem_1_alu_res_o), .sel(bypass_black_box_1_p8));  // open: in3, out
  Multiplexer #(.select(2), .width(32), .enable("false")) multiplexer_4 (
    .in0(multiplexer_1_out), .in1(registerfile_1_p1), .in2(ex_mem_1_alu_res_o), .out(multiplexer_4_out),
    .sel(bypass_black_box_1_p7));  // open: in3
  SA sa_1 (.SA_32(comparator_black_box_1_p2), .out_2(sa_1_out_2));
  Multiplexer #(.width(4), .enable("false")) multiplexer_5 (
    .in0(id_ex_1_op_o), .in1(4'b0111), .out(multiplexer_5_out), .sel(id_ex_1_ctrl_a_o[20]));
  Multiplexer #(.width(32), .enable("false")) multiplexer_6 (
    .in0(comparator_black_box_1_p2), .in1(if_id_1_pc_o), .out(multiplexer_6_out), .sel(id_ex_1_ctrl_a_o[21]));
  Multiplexer #(.width(5), .enable("false")) multiplexer_7 (
    .in0(sa_1_out_2), .in1(5'b01100), .out(multiplexer_7_out), .sel(id_ex_1_ctrl_a_o[20]));
  // Comparator_Black_Box comparator_black_box_1: pin names not known; wires that end beside it: multiplexer_4_out, comparator_black_box_1_p2, nor_1_out, comparator_black_box_1_p4
  // ALU alu_1: pin names not known; wires that end beside it: multiplexer_4_out, multiplexer_6_out, multiplexer_5_out, multiplexer_7_out, alu_1_p5
  assign bit_extender_1_out = {{31{comparator_black_box_1_p4}}, comparator_black_box_1_p4};  // Bit_Extender bit_extender_1
  Adder #(.width(32)) adder_1 (.a(id_ex_1_imm_o), .b(id_ex_1_pc_o), .out(adder_1_out));  // open: cin, cout
  Multiplexer #(.width(32), .enable("false")) multiplexer_8 (
    .in0(alu_1_p5), .in1(bit_extender_1_out), .out(multiplexer_8_out), .sel(or_2_out));
  EX_MEM ex_mem_1 (
    .target(adder_1_out), .clk(clock_1_out), .ALU_res(multiplexer_8_out), .B(id_ex_1_b_o), .Rd(id_ex_1_rd_o),
    .op(id_ex_1_op_o), .ALU_res_o(ex_mem_1_alu_res_o), .B_o(ex_mem_1_b_o), .Rd_o(bypass_black_box_1_p4),
    .op_o(ex_mem_1_op_o));  // open: target_o
  Bit_Extender #(.in_width(32), .out_width(20)) bit_extender_2 (.in(ex_mem_1_alu_res_o), .out(bit_extender_2_out));
  RAM ram_1 (
    .addr(bit_extender_2_out[7:0]), .data(ram_1_data[7:0]), .sel(in_2[0]), .clk(clock_1_out), .ld(in_3),
    .clr(in_4));
  MEM_WB mem_wb_1 (
    .clk(clock_1_out), .D(ex_mem_1_alu_res_o), .M(ram_1_data), .Rd(bypass_black_box_1_p4),
    .Op(ex_mem_1_op_o), .D_o(mem_wb_1_d_o), .M_o(mem_wb_1_m_o), .Rd_o(registerfile_1_p4));  // open: Op_o
  Multiplexer #(.width(32), .enable("false")) multiplexer_9 (
    .in0(mem_wb_1_d_o), .in1(mem_wb_1_m_o), .out(registerfile_1_p1), .sel(1'b1));
  // Pins of 8 and 20 bits meet at bit_extender_2_out
  // Pins of 8 and 32 bits meet at ram_1_data
  // Pins of 1 and 4 bits meet at in_2

  // Notes on the sheet:
  //   contents of risc_vprogramrom_1 (hex, n*v repeats v):
  //   lui t1, 1 lui t2, 2  add t3, t1, t0 # t2 = t1 +t0 xor t4, t1, t2 or t5, t1, t2 auipc a0, 0 sub t0,
  //   t1, t2 # t0 = t1 - t2
endmodule

module PC (
  input  we,
  input  clk,
  input  clr,
  output [31:0] PC_4,
  output [31:0] PC
);

  wire incrementer_1_p2, incrementer_2_p2, incrementer_3_p2;

  Register #(.width(32)) clk_in (.D(PC_4), .en(we), .clk(clk), .Q(PC), .clr(clr));
  // Incrementer #(.width(32)) incrementer_1: pin names not known; wires that end beside it: PC, incrementer_1_p2
  // Incrementer #(.width(32)) incrementer_2: pin names not known; wires that end beside it: incrementer_1_p2, incrementer_2_p2
  // Incrementer #(.width(32)) incrementer_3: pin names not known; wires that end beside it: incrementer_2_p2, incrementer_3_p2
  // Incrementer #(.width(32)) incrementer_4: pin names not known; wires that end beside it: incrementer_3_p2, PC_4
endmodule

module SA (
  input  [31:0] SA_32,
  output [4:0] out_2
);


  assign out_2 = SA_32[4:0];
endmodule

module IF_ID (
  input  [31:0] inst,
  input  clk,
  input  [31:0] PC4,
  output [31:0] inst_o,
  output [31:0] PC_o
);

  Register #(.width(32)) register_1 (.D(inst), .en(1'b1), .clk(clk), .Q(inst_o), .clr(1'b0));
  Register #(.width(32)) register_2 (.D(PC4), .en(1'b1), .clk(clk), .Q(PC_o), .clr(1'b0));
endmodule

module plus_4 (
  input  [31:0] p_in,
  output [31:0] out_2
);

  wire incrementer_1_p2, incrementer_2_p2, incrementer_3_p2;

  // Incrementer #(.width(32)) incrementer_1: pin names not known; wires that end beside it: p_in, incrementer_1_p2
  // Incrementer #(.width(32)) incrementer_2: pin names not known; wires that end beside it: incrementer_1_p2, incrementer_2_p2
  // Incrementer #(.width(32)) incrementer_3: pin names not known; wires that end beside it: incrementer_2_p2, incrementer_3_p2
  // Incrementer #(.width(32)) incrementer_4: pin names not known; wires that end beside it: incrementer_3_p2, out_2
endmodule

module PC_test (
  input  in_1,
  input  in_2,
  input  in_3,
  input  [4:0] in_4,
  input  [4:0] in_5,
  input  [4:0] in_6,
  output [31:0] out_7,
  output [1:0] out_8,
  output [1:0] out_9
);

  Register #(.width(32)) register_1 (.D(out_7), .en(in_1), .clk(in_2), .Q(out_7), .clr(in_3));
  // Bypass_Black_Box bypass_black_box_1: pin names not known; wires that end beside it: in_6, 1'b1, in_4, 1'b1, in_5, out_8, out_9
endmodule

module ID_EX (
  input  clk,
  input  [31:0] PC_4,
  input  [31:0] A,
  input  [31:0] B,
  input  [31:0] imm,
  input  [21:0] ctrl_A,
  input  [11:0] ctrl_B,
  input  [4:0] Rd,
  input  [3:0] op,
  input  [4:0] rs1,
  input  [4:0] rs2,
  output [31:0] PC_o,
  output [31:0] A_o,
  output [31:0] B_o,
  output [31:0] imm_o,
  output [21:0] ctrl_A_o,
  output [11:0] ctrl_B_o,
  output [4:0] Rd_o,
  output [3:0] op_o,
  output [4:0] rs1_o,
  output [4:0] rs2_o
);

  Register #(.width(32)) register_1 (.D(PC_4), .en(1'b1), .clk(clk), .Q(PC_o), .clr(1'b0));
  Register #(.width(32)) register_2 (.D(A), .en(1'b1), .clk(clk), .Q(A_o), .clr(1'b0));
  Register #(.width(32)) register_3 (.D(B), .en(1'b1), .clk(clk), .Q(B_o), .clr(1'b0));
  Register #(.width(32)) register_4 (.D(imm), .en(1'b1), .clk(clk), .Q(imm_o), .clr(1'b0));
  Register #(.width(22)) register_5 (.D(ctrl_A), .en(1'b1), .clk(clk), .Q(ctrl_A_o), .clr(1'b0));
  Register #(.width(12)) register_6 (.D(ctrl_B), .en(1'b1), .clk(clk), .Q(ctrl_B_o), .clr(1'b0));
  Register #(.width(5)) register_7 (.D(Rd), .en(1'b1), .clk(clk), .Q(Rd_o), .clr(1'b0));
  Register #(.width(4)) register_8 (.D(op), .en(1'b1), .clk(clk), .Q(op_o), .clr(1'b0));
  Register #(.width(5)) register_9 (.D(rs1), .en(1'b1), .clk(clk), .Q(rs1_o), .clr(1'b0));
  Register #(.width(5)) register_10 (.D(rs2), .en(1'b1), .clk(clk), .Q(rs2_o), .clr(1'b0));
endmodule

module EX_MEM (
  input  [31:0] target,
  input  clk,
  input  [31:0] ALU_res,
  input  [31:0] B,
  input  [4:0] Rd,
  input  [3:0] op,
  output [31:0] target_o,
  output [31:0] ALU_res_o,
  output [31:0] B_o,
  output [4:0] Rd_o,
  output [3:0] op_o
);

  Register #(.width(32)) register_1 (.D(target), .en(1'b1), .clk(clk), .Q(target_o), .clr(1'b0));
  Register #(.width(32)) register_2 (.D(ALU_res), .en(1'b1), .clk(clk), .Q(ALU_res_o), .clr(1'b0));
  Register #(.width(32)) register_3 (.D(B), .en(1'b1), .clk(clk), .Q(B_o), .clr(1'b0));
  Register #(.width(5)) register_4 (.D(Rd), .en(1'b1), .clk(clk), .Q(Rd_o), .clr(1'b0));
  Register #(.width(4)) register_5 (.D(op), .en(1'b1), .clk(clk), .Q(op_o), .clr(1'b0));
endmodule

module MEM_WB (
  input  clk,
  input  [31:0] D,
  input  [31:0] M,
  input  [4:0] Rd,
  input  [3:0] Op,
  output [31:0] D_o,
  output [31:0] M_o,
  output [4:0] Rd_o,
  output [3:0] Op_o
);

  Register #(.width(32)) register_1 (.D(D), .en(1'b1), .clk(clk), .Q(D_o), .clr(1'b0));
  Register #(.width(32)) register_2 (.D(M), .en(1'b1), .clk(clk), .Q(M_o), .clr(1'b0));
  Register #(.width(5)) register_3 (.D(Rd), .en(1'b1), .clk(clk), .Q(Rd_o), .clr(1'b0));
  Register #(.width(4)) register_4 (.D(Op), .en(1'b1), .clk(clk), .Q(Op_o), .clr(1'b0));
endmodule
